// Logisim project OneBit.circ as structural Verilog: 9 circuits, main circuit main
module main (
  input  W,
  input  R,
  input  in_3,
  input  W_2,
  input  R_2,
  input  Address,
  input  W_3,
  input  R_3,
  input  _0,
  input  _1,
  input  _2,
  input  W_4,
  input  R_4,
  input  Data,
  input  Clock
);

  wire Bus_memory, Bus_write_data, decoder_3_8_1__0_2, decoder_3_8_1__1_2, decoder_3_8_1__2_2,
       decoder_3_8_1__3, decoder_3_8_1__4, decoder_3_8_1__5, decoder_3_8_1__6, decoder_3_8_1__7, or_1_out,
       Ram_cell_0, Ram_cell_1, Ram_write_data, X_memory, X_write_data, Y_memory, Y_write_data;

  Decoder_3_8 decoder_3_8_1 (
    ._0(_0), ._1(_1), ._2(_2), ._0_2(decoder_3_8_1__0_2), ._1_2(decoder_3_8_1__1_2),
    ._2_2(decoder_3_8_1__2_2), ._3(decoder_3_8_1__3), ._4(decoder_3_8_1__4), ._5(decoder_3_8_1__5),
    ._6(decoder_3_8_1__6), ._7(decoder_3_8_1__7));
  // Probe on Ram_cell_0
  Ram Ram (
    .Read(R), .Read_Data(or_1_out), .Write(W), .Write_Data(Ram_write_data), .Address(Address),
    .Cell_0(Ram_cell_0), .Cell_1(Ram_cell_1));
  // Probe on Ram_cell_1
  or or_1 (or_1_out, Ram_write_data, in_3, Bus_write_data, Y_write_data, X_write_data);
  Register X (.Read(R_2), .Read_Data(or_1_out), .Write(W_2), .Write_Data(X_write_data), .Memory(X_memory));
  // Probe on X_memory
  // Probe on Y_memory
  Register Y (.Read(R_3), .Read_Data(or_1_out), .Write(W_3), .Write_Data(Y_write_data), .Memory(Y_memory));
  Register Bus (.Read(R_4), .Read_Data(or_1_out), .Write(W_4), .Write_Data(Bus_write_data), .Memory(Bus_memory));
  // Probe on Bus_memory

  // Notes on the sheet:
  //   Nop
  //   Rom-A (Const)
  //   Rom-X (Const)
  //   Rom-Y (Const)
  //   Sum (Result)
  //   A-XY (X-Y)
  //   Ram-A (Address)
  //   A-Ram (Address)
  //   Data Bus
endmodule

module Register (
  input  Read,
  input  Read_Data,
  input  Write,
  output Memory,
  output Write_Data
);

  wire nand_1_out, nand_2_out, nand_3_out, nand_4_out, nand_5_out, not_2_out;

  nand nand_1 (nand_1_out, Read, Read_Data);
  not not_1 (Write_Data, nand_2_out);
  nand nand_2 (nand_2_out, Memory, Write);
  not not_2 (not_2_out, nand_1_out);
  nand nand_3 (nand_3_out, nand_1_out, Read);
  nand nand_4 (nand_4_out, Read, not_2_out);
  nand nand_5 (nand_5_out, nand_3_out, Memory);
  nand nand_6 (Memory, nand_5_out, nand_4_out);
endmodule

module Ram (
  input  Read,
  input  Read_Data,
  input  Write,
  input  Address,
  output Cell_0,
  output Cell_1,
  output Write_Data
);

  wire Cell_0_write_data, Cell_1_write_data, nor_1_out, nor_2_out, nor_3_out, nor_4_out, not_1_out,
       not_2_out, not_3_out;

  or or_1 (Write_Data, Cell_0_write_data, Cell_1_write_data);
  not not_1 (not_1_out, Write);
  nor nor_1 (nor_1_out, not_2_out, not_1_out);
  nor nor_2 (nor_2_out, not_1_out, Address);
  Register u_Cell_0 (
    .Read(nor_4_out), .Read_Data(Read_Data), .Write(nor_2_out), .Write_Data(Cell_0_write_data),
    .Memory(Cell_0));
  Register u_Cell_1 (
    .Read(nor_3_out), .Read_Data(Read_Data), .Write(nor_1_out), .Write_Data(Cell_1_write_data),
    .Memory(Cell_1));
  not not_2 (not_2_out, Address);
  not not_3 (not_3_out, Read);
  nor nor_3 (nor_3_out, not_2_out, not_3_out);
  nor nor_4 (nor_4_out, not_3_out, Address);
endmodule

module Decoder_3_8 (
  input  _0,
  input  _1,
  input  _2,
  output _0_2,
  output _1_2,
  output _2_2,
  output _3,
  output _4,
  output _5,
  output _6,
  output _7
);

  wire not_1_out, not_2_out, not_3_out;

  not not_1 (not_1_out, _0);
  not not_2 (not_2_out, _1);
  not not_3 (not_3_out, _2);
  and and_1 (_0_2, not_1_out, not_2_out, not_3_out);
  and and_2 (_1_2, _0, not_2_out, not_3_out);
  and and_3 (_2_2, not_1_out, not_3_out, _1);
  and and_4 (_3, not_3_out, _0, _1);
  and and_5 (_4, not_1_out, not_2_out, _2);
  and and_6 (_5, not_2_out, _0, _2);
  and and_7 (_6, not_1_out, _1, _2);
  and and_8 (_7, _0, _1, _2);
endmodule

module D_Trigger (
  input  D,
  input  C,
  output Q,
  output NQ
);

  wire and_1_out, and_2_out, not_1_out;

  not not_1 (not_1_out, D);
  and and_1 (and_1_out, D, C);
  and and_2 (and_2_out, C, not_1_out);
  SR_Trigger sr_trigger_1 (.S(and_1_out), .R(and_2_out), .Q(Q), .NQ(NQ));
endmodule

module T_Trigger (
  input  T,
  output Q
);

  wire d_trigger_1_nq, d_trigger_2_q, not_1_out;

  D_Trigger d_trigger_1 (.D(d_trigger_2_q), .C(T), .NQ(d_trigger_1_nq));  // open: Q
  not not_1 (not_1_out, T);
  D_Trigger d_trigger_2 (.D(d_trigger_1_nq), .C(not_1_out), .Q(d_trigger_2_q), .NQ(Q));
endmodule

module SR_Trigger (
  input  S,
  input  R,
  output Q,
  output NQ
);

  S_R_Flip_Flop #(.trigger("high")) s_r_ff_1 (.S(S), .clk(1'b1), .R(R), .Q(Q), .Qn(NQ));  // open: preset, reset, en
endmodule

module Rom (
  input  in_1
);

  wire decoder_3_8_1__0_2, decoder_3_8_1__1_2, decoder_3_8_1__2_2, decoder_3_8_1__3, decoder_3_8_1__4,
       decoder_3_8_1__5, decoder_3_8_1__6, decoder_3_8_1__7, t_trigger_1_q, t_trigger_2_q, t_trigger_3_q;

  T_Trigger t_trigger_1 (.T(t_trigger_2_q), .Q(t_trigger_1_q));
  T_Trigger t_trigger_2 (.T(in_1), .Q(t_trigger_2_q));
  T_Trigger t_trigger_3 (.T(t_trigger_1_q), .Q(t_trigger_3_q));
  Decoder_3_8 decoder_3_8_1 (
    ._0(t_trigger_2_q), ._1(t_trigger_1_q), ._2(t_trigger_3_q), ._0_2(decoder_3_8_1__0_2),
    ._1_2(decoder_3_8_1__1_2), ._2_2(decoder_3_8_1__2_2), ._3(decoder_3_8_1__3), ._4(decoder_3_8_1__4),
    ._5(decoder_3_8_1__5), ._6(decoder_3_8_1__6), ._7(decoder_3_8_1__7));
endmodule

module Decoder (
  input  _0,
  input  _1,
  input  _2,
  input  Data,
  input  Clock,
  output A_Read,
  output A_Write,
  output Y_Read,
  output X_Read,
  output Sum,
  output Sum_Result,
  output Ram_Read,
  output Ram_Write,
  output Ram_Address,
  output Bus
);

  wire and_1_out, and_2_out, decoder_3_8_1__0_2, decoder_3_8_1__1_2, decoder_3_8_1__2_2, decoder_3_8_1__3,
       decoder_3_8_1__4, decoder_3_8_1__5, decoder_3_8_1__7, not_1_out, or_1_out, or_3_out, or_4_out,
       or_5_out, or_6_out;

  Decoder_3_8 decoder_3_8_1 (
    ._0(_0), ._1(_1), ._2(_2), ._0_2(decoder_3_8_1__0_2), ._1_2(decoder_3_8_1__1_2),
    ._2_2(decoder_3_8_1__2_2), ._3(decoder_3_8_1__3), ._4(decoder_3_8_1__4), ._5(decoder_3_8_1__5),
    ._6(Ram_Write), ._7(decoder_3_8_1__7));
  not not_1 (not_1_out, Data);
  or or_1 (or_1_out, decoder_3_8_1__7, Ram_Write);
  and and_1 (and_1_out, Data, decoder_3_8_1__5);
  and and_2 (and_2_out, decoder_3_8_1__5, not_1_out);
  and and_3 (Ram_Address, or_1_out, Data);
  or or_2 (A_Write, decoder_3_8_1__7, decoder_3_8_1__5);
  or or_3 (or_3_out, decoder_3_8_1__1_2, decoder_3_8_1__2_2, decoder_3_8_1__3);
  and and_4 (Bus, or_3_out, Data);
  or or_4 (or_4_out, decoder_3_8_1__1_2, Ram_Write);
  and and_5 (Sum_Result, decoder_3_8_1__4, Data);
  or or_5 (or_5_out, decoder_3_8_1__2_2, and_1_out);
  or or_6 (or_6_out, decoder_3_8_1__3, and_2_out);
  and and_6 (A_Read, Clock, or_4_out);
  and and_7 (Y_Read, Clock, or_5_out);
  and and_8 (X_Read, Clock, or_6_out);
  and and_9 (Sum, Clock, decoder_3_8_1__4);
  and and_10 (Ram_Read, Clock, decoder_3_8_1__7);

  // Notes on the sheet:
  //   Nop
  //   Rom-A (Const)
  //   Rom-X (Const)
  //   Rom-Y (Const)
  //   Sum (Result)
  //   A-XY (X-Y)
  //   Ram-A (Address)
  //   A-Ram (Address)
endmodule
